// Logisim project SmartLocker.circ as structural Verilog: 1 circuit, main circuit main
module main (
  input  in_1
);

  wire and_1_out, and_2_out, and_3_out, and_4_out, and_5_out, clock_1_out, counter_1_carry, counter_2_q,
       counter_3_carry, d_ff_1_q, d_ff_2_q, d_ff_3_q, d_ff_4_q, d_ff_5_q, d_ff_6_q, not_1_out, not_2_out,
       not_3_out, not_4_out, not_5_out, or_1_out, or_2_out, Owner_Reset_out, Reset_out;

  D_Flip_Flop d_ff_1 (.clk(and_1_out), .D(in_1), .Q(d_ff_1_q), .reset(or_1_out));  // open: Qn, preset, en
  Button Owner_Reset (.out(Owner_Reset_out));
  Button Reset (.out(Reset_out));
  and and_1 (and_1_out, not_1_out, clock_1_out);
  Clock clock_1 (.out(clock_1_out));
  D_Flip_Flop d_ff_2 (.clk(and_1_out), .D(d_ff_1_q), .Q(d_ff_2_q), .reset(or_1_out));  // open: Qn, preset, en
  or or_1 (or_1_out, Owner_Reset_out, or_2_out);
  or or_2 (or_2_out, and_4_out, Reset_out);
  not not_1 (not_1_out, and_4_out);
  D_Flip_Flop d_ff_3 (.clk(and_1_out), .D(d_ff_2_q), .Q(d_ff_3_q), .reset(or_1_out));  // open: Qn, preset, en
  D_Flip_Flop d_ff_4 (.clk(and_1_out), .D(d_ff_3_q), .Q(d_ff_4_q), .reset(or_1_out));  // open: Qn, preset, en
  Counter #(.max('h2)) counter_1 (
    .carry(counter_1_carry), .clk(Reset_out), .clr(Owner_Reset_out));  // open: load, D, count, Q
  D_Flip_Flop d_ff_5 (.clk(and_1_out), .D(d_ff_4_q), .Q(d_ff_5_q), .reset(or_1_out));  // open: Qn, preset, en
  not not_2 (not_2_out, d_ff_2_q);
  Counter #(.width(1), .max('h1)) counter_2 (
    .Q(counter_2_q), .clk(counter_1_carry), .clr(Owner_Reset_out));  // open: load, D, count, carry
  D_Flip_Flop d_ff_6 (.clk(and_1_out), .D(d_ff_5_q), .Q(d_ff_6_q), .reset(or_1_out));  // open: Qn, preset, en
  not not_3 (not_3_out, d_ff_6_q);
  not not_4 (not_4_out, d_ff_3_q);
  not not_5 (not_5_out, counter_1_carry);
  Counter #(.max('h6)) counter_3 (.carry(counter_3_carry), .clk(and_1_out), .clr(or_1_out));  // open: load, D, count, Q
  and and_2 (and_2_out, d_ff_1_q, d_ff_4_q, d_ff_5_q);
  and and_3 (and_3_out, not_3_out, not_4_out, not_2_out);
  and and_4 (and_4_out, counter_2_q, not_5_out);
  and and_5 (and_5_out, counter_3_carry, and_2_out, and_3_out);
  LED UNLOCK (.in(and_5_out));
  LED ALARM (.in(and_4_out));

  // Notes on the sheet:
  //   CLOCK
  //   Durga Chapagai
endmodule
